// Logisim project angulaire.circ as structural Verilog: 5 circuits, main circuit main
module main (
  input  CHA,
  input  CHB,
  input  CHC,
  input  reset,
  output Selected,
  output VDD,
  output GND
);

  wire clock_1_out, comparator_1_eq, comparator_2_eq, d_ff_1_q, d_ff_2_q, debounce_1_filtered,
       debounce_2_filtered, decodeur_1_dir_reset, decodeur_1_dir_set, decodeur_1_en_cnt, dir, en_cnt,
       or_1_out;
  wire [3:0] counter_1_q;
  wire [6:0] encodeur_seven_seg_1_seg;

  Clock clock_1 (.out(clock_1_out));
  or or_1 (or_1_out, reset, comparator_1_eq);
  Counter #(.max('hf), .width(4)) counter_1 (
    .clr(or_1_out), .load(comparator_2_eq), .up(dir), .count(en_cnt), .clk(clock_1_out), .D(4'b1001),
    .Q(counter_1_q));  // open: carry
  debounce debounce_1 (.raw(CHA), .clck(clock_1_out), .filtered(debounce_1_filtered));
  debounce debounce_2 (.raw(CHB), .clck(clock_1_out), .filtered(debounce_2_filtered));
  debounce debounce_3 (.raw(CHC), .clck(clock_1_out), .filtered(Selected));
  D_Flip_Flop d_ff_1 (.D(debounce_1_filtered), .clk(clock_1_out), .Q(d_ff_1_q), .reset(reset));  // open: Qn, preset
  D_Flip_Flop d_ff_2 (.D(debounce_2_filtered), .clk(clock_1_out), .Q(d_ff_2_q), .reset(reset));  // open: Qn, preset
  Comparator #(.mode("unsigned"), .width(4)) comparator_1 (
    .a(counter_1_q), .b(4'b1010), .eq(comparator_1_eq));  // open: gt, lt
  Comparator #(.mode("unsigned"), .width(4)) comparator_2 (
    .a(counter_1_q), .b(4'b1111), .eq(comparator_2_eq));  // open: gt, lt
  S_R_Flip_Flop s_r_ff_1 (
    .S(decodeur_1_dir_set), .R(decodeur_1_dir_reset), .clk(clock_1_out), .Q(dir));  // open: reset, Qn, preset
  decodeur decodeur_1 (
    .Bp(d_ff_2_q), .Ap(d_ff_1_q), .Bc(debounce_2_filtered), .Ac(debounce_1_filtered),
    .dir_set(decodeur_1_dir_set), .en_cnt(decodeur_1_en_cnt), .dir_reset(decodeur_1_dir_reset));
  encodeur_seven_seg encodeur_seven_seg_1 (.A(counter_1_q), .seg(encodeur_seven_seg_1_seg));
  _7_Segment_Display L_7_Segment_Display_1 (
    .g(encodeur_seven_seg_1_seg[6]), .f(encodeur_seven_seg_1_seg[5]), .a(encodeur_seven_seg_1_seg[0]),
    .b(encodeur_seven_seg_1_seg[1]), .e(encodeur_seven_seg_1_seg[4]), .d(encodeur_seven_seg_1_seg[3]),
    .c(encodeur_seven_seg_1_seg[2]));  // open: dp
  wait_2_ticks wait_2_ticks_1 (.reset(reset), .count(decodeur_1_en_cnt), .clck(clock_1_out), .enable(en_cnt));

  assign GND = 1'b0;
  assign VDD = 1'b1;
endmodule

module debounce (
  input  raw,
  input  clck,
  output filtered
);

  wire and_1_out, and_2_out, d_ff_1_q, d_ff_2_q, d_ff_3_q, d_ff_4_q;

  D_Flip_Flop d_ff_1 (.D(raw), .clk(clck), .Q(d_ff_1_q));  // open: Qn, preset, reset
  D_Flip_Flop d_ff_2 (.D(d_ff_1_q), .clk(clck), .Q(d_ff_2_q));  // open: Qn, preset, reset
  D_Flip_Flop d_ff_3 (.D(d_ff_2_q), .clk(clck), .Q(d_ff_3_q));  // open: Qn, preset, reset
  D_Flip_Flop d_ff_4 (.D(d_ff_3_q), .clk(clck), .Q(d_ff_4_q));  // open: Qn, preset, reset
  and and_1 (and_1_out, d_ff_2_q, d_ff_3_q, d_ff_4_q);
  and and_2 (and_2_out, ~d_ff_4_q, ~d_ff_3_q, ~d_ff_2_q);  // AND_Gate
  J_K_Flip_Flop j_k_ff_1 (.J(and_1_out), .K(and_2_out), .clk(clck), .Q(filtered));  // open: Qn, preset, reset
endmodule

module decodeur (
  input  Bp,
  input  Ap,
  input  Bc,
  input  Ac,
  output dir_set,
  output en_cnt,
  output dir_reset
);

  wire and_1_out, and_2_out, and_3_out, and_4_out, and_5_out, and_6_out, and_7_out, and_8_out, and_9_out,
       and_10_out, and_11_out, and_12_out, and_13_out, and_14_out, and_15_out, and_16_out, not_1_out,
       not_2_out, not_3_out, not_4_out;

  not not_1 (not_1_out, Bp);
  not not_2 (not_2_out, Ap);
  not not_3 (not_3_out, Bc);
  not not_4 (not_4_out, Ac);
  and and_1 (and_1_out, not_1_out, not_2_out, not_3_out, Ac);
  and and_2 (and_2_out, not_1_out, Ap, Bc, Ac);
  and and_3 (and_3_out, Bp, not_2_out, not_3_out, not_4_out);
  and and_4 (and_4_out, Bp, Ap, Bc, not_4_out);
  and and_5 (and_5_out, not_1_out, not_2_out, not_3_out, Ac);
  and and_6 (and_6_out, not_1_out, not_2_out, Bc, not_4_out);
  and and_7 (and_7_out, not_1_out, Ap, not_3_out, not_4_out);
  and and_8 (and_8_out, not_1_out, Ap, Bc, Ac);
  and and_9 (and_9_out, Bp, not_2_out, not_3_out, not_4_out);
  and and_10 (and_10_out, Bp, not_2_out, Bc, Ac);
  and and_11 (and_11_out, Bp, Ap, not_3_out, Ac);
  and and_12 (and_12_out, Bp, Ap, Bc, not_4_out);
  and and_13 (and_13_out, not_1_out, not_2_out, Bc, not_4_out);
  and and_14 (and_14_out, not_1_out, Ap, not_3_out, not_4_out);
  and and_15 (and_15_out, Bp, not_2_out, Bc, Ac);
  and and_16 (and_16_out, Bp, Ap, not_3_out, Ac);
  or or_1 (dir_set, and_1_out, and_2_out, and_3_out, and_4_out);
  or or_2 (en_cnt, and_5_out, and_6_out, and_7_out, and_8_out, and_9_out, and_10_out, and_11_out, and_12_out);
  or or_3 (dir_reset, and_13_out, and_14_out, and_15_out, and_16_out);
endmodule

module encodeur_seven_seg (
  input  [3:0] A,
  output [6:0] seg
);

  wire and_1_out, and_2_out, and_3_out, and_4_out, and_5_out, and_6_out, and_7_out, and_8_out, and_9_out,
       and_10_out, and_11_out, and_12_out, and_13_out, and_14_out, and_15_out, and_16_out, not_1_out,
       not_2_out, not_3_out;

  not not_1 (not_1_out, A[2]);
  not not_2 (not_2_out, A[1]);
  not not_3 (not_3_out, A[0]);
  and and_1 (and_1_out, not_1_out, A[1]);
  and and_2 (and_2_out, A[2], not_2_out);
  and and_3 (and_3_out, A[2], not_3_out);
  and and_4 (and_4_out, not_2_out, not_3_out);
  and and_5 (and_5_out, A[2], not_2_out);
  and and_6 (and_6_out, A[2], not_3_out);
  and and_7 (and_7_out, not_1_out, not_3_out);
  or or_1 (seg[4], and_7_out, and_8_out);
  and and_8 (and_8_out, A[1], not_3_out);
  and and_9 (and_9_out, not_1_out, not_3_out);
  and and_10 (and_10_out, not_1_out, A[1]);
  and and_11 (and_11_out, A[1], not_3_out);
  and and_12 (and_12_out, A[2], not_2_out, A[0]);
  or or_2 (seg[2], not_2_out, A[0], A[2]);
  and and_13 (and_13_out, not_2_out, not_3_out);
  or or_3 (seg[1], not_1_out, and_13_out, and_14_out);
  and and_14 (and_14_out, A[1], A[0]);
  and and_15 (and_15_out, not_1_out, not_3_out);
  and and_16 (and_16_out, A[2], A[0]);
  or or_4 (seg[6], and_1_out, and_2_out, and_3_out, A[3]);
  or or_5 (seg[5], and_4_out, and_5_out, and_6_out, A[3]);
  or or_6 (seg[3], and_9_out, and_10_out, and_11_out, and_12_out);
  or or_7 (seg[0], and_15_out, A[1], and_16_out, A[3]);
endmodule

module wait_2_ticks (
  input  reset,
  input  count,
  input  clck,
  output enable
);

  wire comparator_1_eq, or_1_out;
  wire [1:0] counter_1_q;

  Counter #(.max('h3), .width(2)) counter_1 (
    .clr(or_1_out), .up(1'b1), .count(count), .clk(clck), .Q(counter_1_q));  // open: load, D, carry
  or or_1 (or_1_out, reset, enable);
  Comparator #(.mode("unsigned"), .width(2)) comparator_1 (
    .a(counter_1_q), .b(2'b10), .eq(comparator_1_eq));  // open: gt, lt
  D_Flip_Flop d_ff_1 (.D(comparator_1_eq), .clk(clck), .Q(enable));  // open: Qn, preset, reset
endmodule
